// Logisim project control-logic.circ as structural Verilog: 1 circuit, main circuit control_logic
module control_logic (
  input  [31:0] inst,
  input  BrEq,
  input  BrLt,
  output PCSel,
  output RegWEn,
  output [2:0] ImmSel,
  output BrUn,
  output ASel,
  output BSel,
  output [3:0] ALUSel,
  output MemRW,
  output [1:0] WBSel,
  output CSRSel,
  output CSRWen
);

  wire comparator_3_eq, comparator_6_eq, comparator_7_eq, comparator_10_eq, comparator_11_eq,
       comparator_13_eq, comparator_14_eq, comparator_15_eq, comparator_16_eq, comparator_17_eq, I_f,
       jal_or_jalr, multiplexer_1_out, multiplexer_3_out, not_1_out, not_2_out, or_1_out, R_f, S_f, SB_f,
       U_f, UJ_f;
  wire [2:0] adder_1_out, adder_2_out, adder_3_out, funct3, multiplexer_5_out, multiplexer_6_out,
       multiplexer_7_out, multiplexer_8_out, multiplexer_9_out;
  wire [3:0] adder_4_out, ALUSel_R, ALUSel_U, bit_extender_1_out, bit_extender_2_out, multiplexer_10_out,
       multiplexer_12_out;
  wire [6:0] funct7, opcode;
  wire [31:0] shifter_1_out, shifter_2_out;

  not not_1 (not_1_out, BrLt);
  not not_2 (not_2_out, BrEq);
  or or_1 (or_1_out, not_1_out, BrEq);
  Comparator #(.mode("unsigned"), .width(3)) comparator_1 (.a(funct3), .b(3'b101), .eq(CSRSel));  // open: gt, lt
  Comparator #(.mode("unsigned"), .width(7)) comparator_2 (.a(opcode), .b(7'b1110011), .eq(CSRWen));  // open: gt, lt
  Multiplexer #(.enable("false"), .select(3)) multiplexer_1 (
    .in0(BrEq), .in1(not_2_out), .in4(BrLt), .in5(or_1_out), .in6(BrLt), .in7(or_1_out),
    .out(multiplexer_1_out), .sel(funct3));  // open: in2, in3
  nor nor_1 (RegWEn, S_f, SB_f);
  Comparator #(.mode("unsigned"), .width(7)) comparator_3 (
    .a(opcode), .b(7'b0010111), .eq(comparator_3_eq));  // open: gt, lt
  not not_3 (BSel, R_f);
  Multiplexer #(.enable("false"), .width(2)) multiplexer_2 (.in0(2'b01), .in1(2'b10), .out(WBSel), .sel(jal_or_jalr));
  Multiplexer #(.enable("false")) multiplexer_3 (
    .in0(1'b0), .in1(multiplexer_1_out), .out(multiplexer_3_out), .sel(SB_f));
  Comparator #(.mode("unsigned"), .width(3)) comparator_4 (.a(funct3), .b(3'b101), .gt(BrUn));  // open: eq, lt
  or or_2 (ASel, SB_f, UJ_f, comparator_3_eq);
  Multiplexer #(.enable("false"), .select(3), .width(4)) multiplexer_4 (
    .in0(ALUSel_R), .in3(4'b0000), .in4(ALUSel_U), .in5(4'b0000), .out(ALUSel), .sel(ImmSel));  // open: in1, in2, in6, in7
  or or_3 (PCSel, jal_or_jalr, multiplexer_3_out);
  BitSelector #(.group(7), .width(32)) bitselector_1 (.in(inst), .out(opcode), .sel(3'b000));
  Comparator #(.mode("unsigned"), .width(7)) comparator_5 (.a(opcode), .b(7'b0110011), .eq(R_f));  // open: gt, lt
  Comparator #(.mode("unsigned"), .width(7)) comparator_6 (
    .a(opcode), .b(7'b0000011), .eq(comparator_6_eq));  // open: gt, lt
  Comparator #(.mode("unsigned"), .width(7)) comparator_7 (
    .a(opcode), .b(7'b0010011), .eq(comparator_7_eq));  // open: gt, lt
  Comparator #(.mode("unsigned"), .width(7)) comparator_8 (.a(opcode), .b(7'b0100011), .eq(S_f));  // open: gt, lt
  Comparator #(.mode("unsigned"), .width(7)) comparator_9 (.a(opcode), .b(7'b1100011), .eq(SB_f));  // open: gt, lt
  Comparator #(.mode("unsigned"), .width(7)) comparator_10 (
    .a(opcode), .b(7'b0010111), .eq(comparator_10_eq));  // open: gt, lt
  Comparator #(.mode("unsigned"), .width(7)) comparator_11 (
    .a(opcode), .b(7'b0110111), .eq(comparator_11_eq));  // open: gt, lt
  Comparator #(.mode("unsigned"), .width(7)) comparator_12 (.a(opcode), .b(7'b1101111), .eq(UJ_f));  // open: gt, lt
  or or_4 (I_f, comparator_6_eq, comparator_7_eq);
  or or_5 (U_f, comparator_10_eq, comparator_11_eq);
  Shifter #(.shift("lr"), .width(32)) shifter_1 (.in(inst), .\dist (5'b01100), .out(shifter_1_out));
  Comparator #(.mode("unsigned"), .width(7)) comparator_13 (
    .a(opcode), .b(7'b1100111), .eq(comparator_13_eq));  // open: gt, lt
  BitSelector #(.group(3), .width(32)) bitselector_2 (.in(shifter_1_out), .out(funct3), .sel(4'b0000));
  Multiplexer #(.enable("false"), .width(3)) multiplexer_5 (
    .in0(3'b000), .in1(3'b001), .out(multiplexer_5_out), .sel(I_f));
  Multiplexer #(.enable("false"), .width(3)) multiplexer_6 (
    .in0(3'b000), .in1(3'b010), .out(multiplexer_6_out), .sel(S_f));
  Multiplexer #(.enable("false"), .width(3)) multiplexer_7 (
    .in0(3'b000), .in1(3'b011), .out(multiplexer_7_out), .sel(SB_f));
  Multiplexer #(.enable("false"), .width(3)) multiplexer_8 (
    .in0(3'b000), .in1(3'b100), .out(multiplexer_8_out), .sel(U_f));
  Multiplexer #(.enable("false"), .width(3)) multiplexer_9 (
    .in0(3'b000), .in1(3'b101), .out(multiplexer_9_out), .sel(UJ_f));
  or or_6 (jal_or_jalr, UJ_f, comparator_13_eq);
  Adder #(.width(3)) adder_1 (.a(multiplexer_5_out), .b(multiplexer_6_out), .out(adder_1_out));  // open: cin, cout
  Adder #(.width(3)) adder_2 (.a(multiplexer_7_out), .b(multiplexer_8_out), .out(adder_2_out));  // open: cin, cout
  assign bit_extender_1_out = {{1{1'b0}}, funct3};  // Bit_Extender bit_extender_1
  Shifter #(.shift("lr"), .width(32)) shifter_2 (.in(inst), .\dist (5'b11001), .out(shifter_2_out));
  Adder #(.width(3)) adder_3 (.a(adder_1_out), .b(adder_2_out), .out(adder_3_out));  // open: cin, cout
  Adder #(.width(4)) adder_4 (.a(bit_extender_1_out), .b(4'b1000), .out(adder_4_out));  // open: cin, cout
  BitSelector #(.group(7), .width(32)) bitselector_3 (.in(shifter_2_out), .out(funct7), .sel(3'b000));
  Adder #(.width(3)) adder_5 (.a(adder_3_out), .b(multiplexer_9_out), .out(ImmSel));  // open: cin, cout
  Multiplexer #(.enable("false"), .width(4)) multiplexer_10 (
    .in0(4'b1100), .in1(4'b1101), .out(multiplexer_10_out), .sel(comparator_14_eq));
  Comparator #(.width(3)) comparator_14 (.a(funct3), .b(3'b101), .eq(comparator_14_eq));  // open: gt, lt
  Comparator #(.width(7)) comparator_15 (.a(funct7), .b(7'b0000001), .eq(comparator_15_eq));  // open: gt, lt
  Multiplexer #(.enable("false"), .width(4)) multiplexer_11 (
    .in0(4'b0000), .in1(4'b1111), .out(ALUSel_U), .sel(comparator_16_eq));
  Comparator #(.width(7)) comparator_16 (.a(opcode), .b(7'b0110111), .eq(comparator_16_eq));  // open: gt, lt
  Multiplexer #(.enable("false"), .width(4)) multiplexer_12 (
    .in0(multiplexer_10_out), .in1(adder_4_out), .out(multiplexer_12_out), .sel(comparator_15_eq));
  Multiplexer #(.enable("false"), .width(4)) multiplexer_13 (
    .in0(multiplexer_12_out), .in1(bit_extender_2_out), .out(ALUSel_R), .sel(comparator_17_eq));
  assign bit_extender_2_out = {{1{1'b0}}, funct3};  // Bit_Extender bit_extender_2
  Comparator #(.width(7)) comparator_17 (.a(funct7), .b({7{1'b0}}), .eq(comparator_17_eq));  // open: gt, lt

  // Other names for the same wires on the sheet: inst_type[2:0] = ImmSel

  // Notes on the sheet:
  //   INPUTS to your circuit
  //   DON'T CHANGE THE LOCATIONS OF THE INPUTS AND OUTPUTS!
  //   OUTPUT from your circuit
endmodule
