// Logisim project cpu.circ as structural Verilog: 1 circuit, main circuit cpu
module cpu (
  input  clk,
  input  [31:0] INSTRUCTION,
  input  [31:0] READ_DATA,
  output [31:0] WRITE_ADDRESS,
  output [31:0] PROGRAM_COUNTER,
  output [31:0] ra,
  output [31:0] sp,
  output [31:0] t0,
  output [31:0] t1,
  output [31:0] t2,
  output [31:0] s0,
  output [31:0] s1,
  output [31:0] a0,
  output [31:0] tohost,
  output [3:0] WRITE_ENABLE,
  output [31:0] WRITE_DATA
);

  wire ASel, BrEq, BrLt, BrUn, BSel, CSRSel, CSRWen, MemRW, PCSel, RegWEn;
  wire [1:0] WBSel;
  wire [2:0] ImmSel;
  wire [3:0] ALUSel;
  wire [4:0] bitselector_1_out, bitselector_2_out, bitselector_3_out;
  wire [11:0] bitselector_4_out;
  wire [31:0] bit_extender_1_out, CSRSrc, Imm, multiplexer_1_out, multiplexer_4_out, multiplexer_5_out,
       NEXT_PC, rd, rs1, shifter_1_out, shifter_2_out;

  Adder #(.width(32)) adder_1 (.a(PROGRAM_COUNTER), .b(32'h4), .out(NEXT_PC));  // open: cin, cout
  Multiplexer #(.enable("false"), .width(32)) multiplexer_1 (
    .in0(NEXT_PC), .in1(WRITE_ADDRESS), .out(multiplexer_1_out), .sel(PCSel));
  Register #(.width(32)) PC (.D(multiplexer_1_out), .en(1'b1), .clk(clk), .Q(PROGRAM_COUNTER));  // open: clr
  BitSelector #(.group(5), .width(32)) bitselector_1 (.in(shifter_1_out), .out(bitselector_1_out), .sel(3'b000));
  Shifter #(.shift("lr"), .width(32)) shifter_1 (.in(INSTRUCTION), .\dist (5'b01111), .out(shifter_1_out));
  BitSelector #(.group(5), .width(32)) bitselector_2 (.in(shifter_1_out), .out(bitselector_2_out), .sel(3'b001));
  BitSelector #(.group(5), .width(32)) bitselector_3 (.in(shifter_2_out), .out(bitselector_3_out), .sel(3'b000));
  Shifter #(.shift("lr"), .width(32)) shifter_2 (.in(INSTRUCTION), .\dist (5'b00111), .out(shifter_2_out));
  assign bit_extender_1_out = {{27{1'b0}}, bitselector_1_out};  // Bit_Extender bit_extender_1
  imm_gen imm_gen_1 (.inst(INSTRUCTION), .ImmSel(ImmSel), .imm(Imm));
  BitSelector #(.group(12), .width(32)) bitselector_4 (.in(Imm), .out(bitselector_4_out), .sel(2'b00));
  Multiplexer #(.enable("false"), .width(32)) multiplexer_2 (
    .in0(rs1), .in1(bit_extender_1_out), .out(CSRSrc), .sel(CSRSel));
  regfile regfile_1 (
    .rs1(bitselector_1_out), .rs2(bitselector_2_out), .rd(bitselector_3_out), .Write_Data(rd),
    .RegWEn(RegWEn), .clk(clk), .ra(ra), .sp(sp), .t0(t0), .t1(t1), .t2(t2), .s0(s0), .s1(s1), .a0(a0),
    .Read_Data_1(rs1), .Read_Data_2(WRITE_DATA));
  // csr csr_1: pin names not known; wires that end beside it: bitselector_4_out, CSRSrc, CSRWen, clk, tohost
  control_logic control_logic_1 (
    .CSRWen(CSRWen), .PCSel(PCSel), .RegWEn(RegWEn), .ImmSel(ImmSel), .BrUn(BrUn), .ASel(ASel), .BSel(BSel),
    .ALUSel(ALUSel), .MemRW(MemRW), .WBSel(WBSel), .CSRSel(CSRSel), .inst(INSTRUCTION), .BrEq(BrEq),
    .BrLt(BrLt));
  Multiplexer #(.enable("false"), .select(2), .width(32)) multiplexer_3 (
    .in0(READ_DATA), .in1(WRITE_ADDRESS), .in2(NEXT_PC), .out(rd), .sel(WBSel));  // open: in3
  branch_comp branch_comp_1 (.rs1(rs1), .rs2(WRITE_DATA), .BrUn(BrUn), .BrEq(BrEq), .BrLt(BrLt));
  Multiplexer #(.enable("false"), .width(32)) multiplexer_4 (
    .in0(rs1), .in1(PROGRAM_COUNTER), .out(multiplexer_4_out), .sel(ASel));
  Multiplexer #(.enable("false"), .width(32)) multiplexer_5 (
    .in0(WRITE_DATA), .in1(Imm), .out(multiplexer_5_out), .sel(BSel));
  alu alu_1 (.Result(WRITE_ADDRESS), .A(multiplexer_4_out), .B(multiplexer_5_out), .ALUSel(ALUSel));

  // Other names for the same wires on the sheet: ALUResult[31:0] = WRITE_ADDRESS; rs2[31:0] = WRITE_DATA

  // Notes on the sheet:
  //   Output to IMEM
  //   IMEM (do **NOT** move this)
  //   Inputs from IMEM
  //   It is OK to move the PC, RegFile, ALU, MEM, Branch Comp, Imm Gen, and Control Logic to wherever is most convenient for you when constructing your CPU, and to delete this text
  //   Inputs/Outputs for testing. Do **NOT** move these.
  //   Outputs To DMEM
  //   DMEM (do **NOT** move this)
  //   Inputs From DMEM
endmodule
