// Logisim project imm-gen.circ as structural Verilog: 1 circuit, main circuit imm_gen
module imm_gen (
  input  [31:0] inst,
  input  [2:0] ImmSel,
  output [31:0] imm
);

  wire comparator_2_eq, comparator_3_eq, i_7, i_20, i_31, I_f, R_f, S_f, SB_f;
  wire [3:0] bitselector_6_out, bitselector_7_out;
  wire [5:0] bitselector_5_out;
  wire [6:0] opcode;
  wire [7:0] bitselector_8_out;
  wire [10:0] bitselector_9_out;
  wire [31:0] bit_extender_1_out, bit_extender_2_out, bit_extender_3_out, bit_extender_4_out,
       bit_extender_5_out, i_11_8, i_19_12, i_24_21, i_30_25, shifter_1_out, shifter_2_out, shifter_3_out,
       shifter_4_out, shifter_5_out;

  BitSelector #(.width(32)) bitselector_1 (.in(inst), .out(i_31), .sel({5{1'b1}}));
  BitSelector #(.width(32)) bitselector_2 (.in(inst), .out(i_20), .sel(5'b10100));
  BitSelector #(.width(32)) bitselector_3 (.in(inst), .out(i_7), .sel(5'b00111));
  BitSelector #(.group(7), .width(32)) bitselector_4 (.in(inst), .out(opcode), .sel(3'b000));
  BitSelector #(.group(6), .width(32)) bitselector_5 (.in(shifter_1_out), .out(bitselector_5_out), .sel(3'b000));
  Shifter #(.shift("lr"), .width(32)) shifter_1 (.in(inst), .\dist (5'b11001), .out(shifter_1_out));
  BitSelector #(.group(4), .width(32)) bitselector_6 (.in(shifter_2_out), .out(bitselector_6_out), .sel(3'b000));
  Shifter #(.shift("lr"), .width(32)) shifter_2 (.in(inst), .\dist (5'b10101), .out(shifter_2_out));
  BitSelector #(.group(4), .width(32)) bitselector_7 (.in(shifter_3_out), .out(bitselector_7_out), .sel(3'b000));
  Shifter #(.shift("lr"), .width(32)) shifter_3 (.in(inst), .\dist (5'b01000), .out(shifter_3_out));
  BitSelector #(.group(8), .width(32)) bitselector_8 (.in(shifter_4_out), .out(bitselector_8_out), .sel(2'b00));
  Shifter #(.shift("lr"), .width(32)) shifter_4 (.in(inst), .\dist (5'b01100), .out(shifter_4_out));
  BitSelector #(.group(11), .width(32)) bitselector_9 (.in(shifter_5_out), .out(bitselector_9_out), .sel(2'b00));
  Shifter #(.shift("lr"), .width(32)) shifter_5 (.in(inst), .\dist (5'b10100), .out(shifter_5_out));
  assign bit_extender_1_out = {{26{1'b0}}, bitselector_5_out};  // Bit_Extender bit_extender_1
  assign bit_extender_2_out = {{28{1'b0}}, bitselector_6_out};  // Bit_Extender bit_extender_2
  assign bit_extender_3_out = {{28{1'b0}}, bitselector_7_out};  // Bit_Extender bit_extender_3
  assign bit_extender_4_out = {{24{1'b0}}, bitselector_8_out};  // Bit_Extender bit_extender_4
  assign bit_extender_5_out = {{21{1'b0}}, bitselector_9_out};  // Bit_Extender bit_extender_5
  Shifter #(.width(32)) shifter_6 (.in(bit_extender_1_out), .\dist (5'b00101), .out(i_30_25));
  Shifter #(.width(32)) shifter_7 (.in(bit_extender_2_out), .\dist (5'b00001), .out(i_24_21));
  Shifter #(.width(32)) shifter_8 (.in(bit_extender_3_out), .\dist (5'b00001), .out(i_11_8));
  Shifter #(.width(32)) shifter_9 (.in(bit_extender_4_out), .\dist (5'b01100), .out(i_19_12));
  Shifter #(.width(32)) shifter_10 (.in(bit_extender_5_out), .\dist (5'b10100), .out(i_19_12));
  Comparator #(.mode("unsigned"), .width(7)) comparator_1 (.a(opcode), .b(7'b0100001), .eq(R_f));  // open: gt, lt
  Comparator #(.mode("unsigned"), .width(7)) comparator_2 (
    .a(opcode), .b(7'b0000011), .eq(comparator_2_eq));  // open: gt, lt
  Comparator #(.mode("unsigned"), .width(7)) comparator_3 (
    .a(opcode), .b(7'b0010011), .eq(comparator_3_eq));  // open: gt, lt
  Comparator #(.mode("unsigned"), .width(7)) comparator_4 (.a(opcode), .b(7'b0100011), .eq(S_f));  // open: gt, lt
  Comparator #(.mode("unsigned"), .width(7)) comparator_5 (.a(opcode), .b(7'b1100011), .eq(SB_f));  // open: gt, lt
  or or_1 (I_f, comparator_2_eq, comparator_3_eq);

  // Notes on the sheet:
  //   INPUTS to your circuit
  //   inst[30:25]
  //   inst[24:21]
  //   inst[11:8]
  //   inst[19:12]
  //   inst[30:20]
  //   DON'T CHANGE THE LOCATIONS OF THE INPUTS AND OUTPUTS!
  //   OUTPUT from your circuit
endmodule
